# Fritzing sketch Projecto_bioreactorAlgas (saved by Fritzing 1.0.4)

parts:
  U1 = RELAY [package=relay-jzc]
  Disp1 = 60mm 8x8 dot matrix row cathode led display with standard pcb pads
  Componente1 = BH1750
  M1 = ph-4502c [package=THT]
  A1 = TS-300B interface
  A2 = TS 300B sensor
  A3 = Arduino Nano ESP32
  Componente2 = OLED Monochrome 128x64 0.96 inch [part_number=326]

nets:
  N1: U1.COIL2, A3.Pin_4
  GND: U1.NC, Disp1.pin_2, Componente1.GND, M1.pin4, M1.pin5, A1.Pin_1, A3.Pin_14, A3.Pin_19, Componente2.GND
  VCC: U1.NO, Disp1.pin_1, Componente1.VCC, M1.pin6, A1.Pin_4, A3.Pin_2, Componente2.3.3V
  N2: Componente1.SCL, A3.Pin_9, Componente2.SCLK_SCK
  N3: Componente1.SDA, A3.Pin_8, Componente2.DC_SA0
  N4: M1.pin3, A3.Pin_29
  N5: A1.Pin_5, A2.Pin_1
  N6: A1.Pin_6, A2.Pin_2
  N7: A1.Pin_7, A2.Pin_3

custom parts:
  BH1750: Light Sensor
  ph-4502c: ph-4502c PH Meter.
  TS-300B interface: TS-300B interface.
  TS 300B sensor: TS 300B water turbidity sensor.
  Arduino Nano ESP32: Arduino® Nano ESP32 tht.
  OLED Monochrome 128x64 0.96 inch: These displays are small, only about 1" diameter, but very readable due to the high contrast of an OLED display. This display is made of 128x64 individual white OLED pixels, each one is turned on or off by the controller chip. Because the display makes its own light, no backlight is required. This reduces the power required to run the OLED and is why the display has such high contrast; we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
